# Fritzing sketch RaspberryPi_v01 (saved by Fritzing 0.9.3b)
circuit board: 13.1392cm x 7.53087cm
breadboards: 2

parts:
  Raspberry_Pi_1 = Raspberry Pi 3 [part_number=RPI-3-V1.2]
  U1 = LCD-16X2 [package=lcd-16x2_noholes]
  U2 = POT [package=alps_pot]
  RHT1 = Humidity and Temperature Sensor RHT03
  RHT2 = Humidity and Temperature Sensor RHT03
  R1 = Resistor [tolerance=±5% resistance=220 package="0603 [SMD]"]
  R2 = Resistor [tolerance=±5% resistance=220 package="0603 [SMD]"]
  S1 = Pushbutton [package="[SMD]"]
  S2 = Momentary Switch [package=ksa_sealed_tac_switch]
  S3 = Pushbutton [package="[SMD]"]
  RHT3 = Humidity and Temperature Sensor RHT03
  R3 = Resistor [tolerance=±5% resistance=220 package="0603 [SMD]"]
  RHT4 = Humidity and Temperature Sensor RHT03
  R4 = Resistor [tolerance=±5% resistance=220 package="0603 [SMD]"]

nets:
  N1: Raspberry_Pi_1.GPIO17, U1.E
  N2: Raspberry_Pi_1.GPIO22, U1.RS
  N3: Raspberry_Pi_1.GPIO5, S3.Pin_3, S3.Pin_4
  N4: Raspberry_Pi_1.GPIO6, S2.3
  N5: Raspberry_Pi_1.GPIO13, S1.Pin_3, S1.Pin_4
  N6: Raspberry_Pi_1.GPIO16, RHT1.Data-signal, R1.Pin_1
  GND: Raspberry_Pi_1.GND, U1.VSS, U1.R_W, U1.K, U2.E, RHT2.GND_2, RHT3.GND_2, RHT4.GND_2
  N7: Raspberry_Pi_1.GPIO12, RHT2.Data-signal, R2.Pin_1
  N8: Raspberry_Pi_1.GPIO7, RHT3.Data-signal, R3.Pin_1
  N9: Raspberry_Pi_1.GPIO8, RHT4.Data-signal, R4.Pin_1
  N10: Raspberry_Pi_1.GPIO25, U1.DB4
  N11: Raspberry_Pi_1.GPIO24, U1.DB5
  N12: Raspberry_Pi_1.GPIO23, U1.DB6
  N13: Raspberry_Pi_1.GPIO18, U1.DB7
  VCC: Raspberry_Pi_1.5V, U1.VDD, U1.A, U2.A, RHT1.Vcc, RHT1.GND_2, RHT2.Vcc, R1.Pin_0, R2.Pin_0, S1.Pin_1, S1.Pin_2, S2.1, S3.Pin_1, S3.Pin_2, RHT3.Vcc, R3.Pin_0, RHT4.Vcc, R4.Pin_0
  N14: U1.VO, U2.S
